# Fritzing sketch AQI (saved by Fritzing 0.9.3b)
breadboards: 1

parts:
  Part1 = Arduino Mega 2560 (Rev3)
  DHT22-Temperature_and_Humidity_sensor = Humidity and Temperature Sensor RHT03
  MQ5-_LPG_Flammable_gas = Gas Sensor Breakout Board
  MQ135(All) = Gas Sensor Breakout Board
  MQ7_-_CO_sensor = Gas Sensor Breakout Board
  MQ8_-_H2_sensor = Gas Sensor Breakout Board

nets:
  N1: Part1.A0, MQ135(All).AOUT
  N2: Part1.A1, MQ7_-_CO_sensor.AOUT
  N3: Part1.A2, MQ8_-_H2_sensor.AOUT
  N4: Part1.A3, MQ5-_LPG_Flammable_gas.AOUT
  GND: Part1.GND, DHT22-Temperature_and_Humidity_sensor.GND_1, MQ5-_LPG_Flammable_gas.GND, MQ135(All).GND, MQ7_-_CO_sensor.GND, MQ8_-_H2_sensor.GND
  5V: Part1.5V, DHT22-Temperature_and_Humidity_sensor.Vcc, MQ5-_LPG_Flammable_gas.5V, MQ135(All).5V, MQ7_-_CO_sensor.5V, MQ8_-_H2_sensor.5V
  N5: Part1.D2_PWM, DHT22-Temperature_and_Humidity_sensor.Data-signal

custom parts:
  Gas Sensor Breakout Board: Gas sensor breakout board. Input voltage is 5V. Sensor output is available in analog and digital.
